# Fritzing sketch 6-LED-Test (saved by Fritzing 0.9.0b)
breadboards: 1

parts:
  LED1 = smd LED [color="Red (633nm)" package="0805 [SMD]"]
  LED2 = smd LED [color="Red (633nm)" package="0805 [SMD]"]
  LED3 = smd LED [color="Red (633nm)" package="0805 [SMD]"]
  LED4 = smd LED [color="Green (565nm)" package="0805 [SMD]"]
  LED5 = smd LED [color="Green (565nm)" package="0805 [SMD]"]
  LED6 = smd LED [color="Green (565nm)" package="0805 [SMD]"]
  R3 = Resistor [tolerance=±5% resistance=560 package=THT]
  R4 = Resistor [tolerance=±5% resistance=560 package=THT]
  R5 = Resistor [tolerance=±5% resistance=560 package=THT]
  R6 = Resistor [tolerance=±5% resistance=560 package=THT]
  R7 = Resistor [tolerance=±5% resistance=560 package=THT]
  Part1 = Arduino Uno (Rev3)
  R8 = Resistor [tolerance=±5% resistance=560 package=THT]

nets:
  N1: LED1.anode, LED2.anode, LED3.anode, LED4.anode, LED5.anode, LED6.anode, R3.Pin_0, R4.Pin_0, R5.Pin_0, R6.Pin_0, R7.Pin_0, Part1.5V, R8.Pin_0
  N2: R3.Pin_1, Part1.D6_PWM
  N3: R4.Pin_1, Part1.D3_PWM
  N4: R5.Pin_1, Part1.D9_PWM
  N5: R6.Pin_1, Part1.D10_PWM/SS
  N6: R7.Pin_1, Part1.D11_PWM/MOSI
  N7: Part1.D5_PWM, R8.Pin_1
