# Fritzing sketch Project_Final (saved by Fritzing 0.9.0b)
breadboards: 3

parts:
  Part1 = Arduino Uno (Rev3)
  K1 = Relay [part_number=HFD27/005-H package=THT]
  D1 = Rectifier Diode [package="Melf DO-213 AA [SMD]"]
  Light_#8 = Power plug
  120V_AC_Power = Power plug
  LED1 = smd LED [color="Red (633nm)" package="0805 [SMD]"]
  R1 = Resistor [tolerance=±5% resistance=560 package="0805 [SMD]"]
  LED2 = smd LED [color="Green (555nm)" package="0805 [SMD]"]
  R2 = Resistor [tolerance=±5% resistance=560 package="0805 [SMD]"]
  R3 = Resistor [tolerance=±5% resistance=560 package="0805 [SMD]"]
  R4 = Resistor [tolerance=±5% resistance=560 package="0805 [SMD]"]
  R5 = Resistor [tolerance=±5% resistance=560 package="0805 [SMD]"]
  R6 = Resistor [tolerance=±5% resistance=560 package="0805 [SMD]"]
  R7 = Resistor [tolerance=±5% resistance=560 package="0805 [SMD]"]
  R8 = Resistor [tolerance=±5% resistance=560 package="0805 [SMD]"]
  LED3 = smd LED [color="Red (633nm)" package="0805 [SMD]"]
  LED4 = smd LED [color="Green (555nm)" package="0805 [SMD]"]
  LED5 = smd LED [color="Red (633nm)" package="0805 [SMD]"]
  LED6 = smd LED [color="Green (555nm)" package="0805 [SMD]"]
  LED7 = smd LED [color="Red (633nm)" package="0805 [SMD]"]
  LED8 = smd LED [color="Green (555nm)" package="0805 [SMD]"]
  K2 = Relay [part_number=HFD27/005-H package=THT]
  K3 = Relay [part_number=HFD27/005-H package=THT]
  K4 = Relay [part_number=HFD27/005-H package=THT]
  K5 = Relay [part_number=HFD27/005-H package=THT]
  K6 = Relay [part_number=HFD27/005-H package=THT]
  D2 = Rectifier Diode [package="Melf DO-213 AA [SMD]"]
  D3 = Rectifier Diode [package="Melf DO-213 AA [SMD]"]
  D4 = Rectifier Diode [package="Melf DO-213 AA [SMD]"]
  D5 = Rectifier Diode [package="Melf DO-213 AA [SMD]"]
  D6 = Rectifier Diode [package="Melf DO-213 AA [SMD]"]
  D7 = Rectifier Diode [package="Melf DO-213 AA [SMD]"]
  D8 = Rectifier Diode [package="Melf DO-213 AA [SMD]"]
  K7 = Relay [part_number=HFD27/005-H package=THT]
  K8 = Relay [part_number=HFD27/005-H package=THT]
  Light_#6 = Power plug
  Light_#5 = Power plug
  Light_#7 = Power plug
  Light_#4 = Power plug
  Light_#3 = Power plug
  Light_#2 = Power plug
  Light_#1 = Power plug

nets:
  N1: Part1.D8, LED7.anode, D7.anode
  N2: Part1.D9_PWM, LED8.anode, D8.anode
  N3: Part1.D2, D1.anode, LED1.anode
  N4: Part1.D3_PWM, LED2.anode, D2.anode
  N5: Part1.D4, LED3.anode, D3.anode
  N6: Part1.D5_PWM, LED4.anode, D4.anode
  N7: Part1.D6_PWM, LED5.anode, D5.anode
  N8: Part1.D7, LED6.anode, D6.anode
  N9: Part1.GND, K1.C1, K1.C2, D1.cathode, R1.Pin_1, R2.Pin_1, R3.Pin_1, R4.Pin_1, R5.Pin_1, R6.Pin_1, R7.Pin_1, R8.Pin_1, K2.C1, K2.C2, K3.C1, K3.C2, K4.C1, K4.C2, K5.C1, K5.C2, K6.C1, K6.C2, D2.cathode, D3.cathode, D4.cathode, D5.cathode, D6.cathode, D7.cathode, D8.cathode, K7.C1, K7.C2, K8.C1, K8.C2
  N10: K1.B, 120V_AC_Power.VCC, K2.B, K3.B, K4.B, K5.B, K6.B, K7.B, K8.B
  GND: Light_#8.GND, 120V_AC_Power.GND, Light_#6.GND, Light_#5.GND, Light_#7.GND, Light_#4.GND, Light_#3.GND, Light_#2.GND, Light_#1.GND
  N11: LED1.cathode, R8.Pin_0
  N12: R1.Pin_0, LED8.cathode
  N13: LED2.cathode, R7.Pin_0
  N14: R2.Pin_0, LED7.cathode
  N15: R3.Pin_0, LED6.cathode
  N16: R4.Pin_0, LED5.cathode
  N17: R5.Pin_0, LED4.cathode
  N18: R6.Pin_0, LED3.cathode
